// Digital circuit 1_bit_register.dig as structural Verilog
module _1_bit_register (
  input  EN,
  input  C,
  input  D,
  output Q
);

  wire multiplexer_1_out;

  Multiplexer multiplexer_1 (.sel(EN), .in_0(Q), .in_1(D), .out(multiplexer_1_out));
  D_FF d_ff_1 (.D(multiplexer_1_out), .C(C), .Q(Q));  // open: nQ

  // Notes on the sheet:
  //   1 Bit Register
endmodule

/* Test case Register_test:
C	EN	D	Q
C	0	0	0
C	0	1	0
C	1	0	0
C	1	1	1
C	1	1	1
C	0	0	1
C	0	1	1
C	1	0	0
*/
